# Fritzing sketch Fish_Circuitry (saved by Fritzing 0.9.3b)
breadboards: 1

parts:
  J1 = Infrared Proximity Sensor
  Part1 = Arduino Uno (Rev3)
  J6 = Basic Servo
  J2 = Basic Servo
  J5 = Basic Servo
  Part2 = Bluetooth HC-05 Macho

nets:
  N1: J1.Vout, Part1.A0
  GND: J1.GND, Part1.GND, J6.gnd, J2.gnd, J5.gnd, Part2.GND
  VCC: J1.Vcc, Part1.5V, J6.vcc, J2.vcc, J5.vcc, Part2.VCC
  N2: Part1.D9_PWM, J2.pulse
  N3: Part1.D10_PWM/SS, J5.pulse
  N4: Part1.D11_PWM/MOSI, J6.pulse
  N5: Part1.D0/RX, Part2.TXD
  N6: Part1.D1/TX, Part2.RXD
  N7: Part1.D3_PWM, Part2.State

// code stored in the sketch: Fritzing.ino

